// Logisim project USR_32Bit.circ as structural Verilog: 3 circuits, main circuit Mux_4to1
module Mux_4to1 (
  input  I0,
  input  I1,
  input  I2,
  input  I3,
  input  S1,
  input  S0,
  output out_7
);

  wire nand_1_out, nand_2_out, nand_3_out, nand_4_out, nand_5_out, nand_6_out;

  nand nand_1 (nand_1_out, S0, S0);
  nand nand_2 (nand_2_out, S1, S1);
  nand nand_3 (nand_3_out, I0, nand_2_out, nand_1_out);
  nand nand_4 (nand_4_out, I1, nand_2_out, S0);
  nand nand_5 (nand_5_out, I2, S1, nand_1_out);
  nand nand_6 (nand_6_out, I3, S1, S0);
  nand nand_7 (out_7, nand_3_out, nand_4_out, nand_5_out, nand_6_out);
endmodule

module USR_1BIT (
  input  No_Connection,
  input  Shift_Right,
  input  Shift_Left,
  input  CLK,
  input  Parallel_Load,
  input  S1,
  input  S0,
  output out_8,
  output Q_bar
);

  wire mux_4to1_1_out_7;

  Mux_4to1 mux_4to1_1 (
    .I0(out_8), .I1(Shift_Right), .I2(Shift_Left), .I3(Parallel_Load), .S1(S1), .S0(S0),
    .out_7(mux_4to1_1_out_7));
  D_Flip_Flop #(.trigger("falling")) d_ff_1 (
    .D(mux_4to1_1_out_7), .clk(CLK), .Q(out_8), .Qn(Q_bar));  // open: preset, reset
endmodule

module USR_32BIT (
  input  Shift_Left,
  input  Shift_Right,
  input  Clk,
  input  S1,
  input  S0,
  input  P24,
  input  P25,
  input  P26,
  input  P27,
  input  P28,
  input  P29,
  input  P31,
  input  P1,
  input  P2,
  input  P4,
  input  P5,
  input  P6,
  input  P7,
  input  P8,
  input  P9,
  input  P10,
  input  P11,
  input  P12,
  input  P13,
  input  P19,
  input  P20,
  input  P22,
  input  P23,
  input  P30,
  input  P0,
  input  P3,
  input  P14,
  input  P15,
  input  P16,
  input  P17,
  input  P18,
  input  P21,
  output Q3,
  output Q4,
  output Q5,
  output Q6,
  output Q9,
  output Q10,
  output Q11,
  output Q12,
  output Q13,
  output Q16,
  output Q17,
  output Q18,
  output Q19,
  output Q20,
  output Q21,
  output Q22,
  output Q23,
  output Q1,
  output Q2,
  output Q7,
  output Q8,
  output Q14,
  output Q15,
  output Q24,
  output Q25,
  output Q26,
  output Q27,
  output Q28,
  output Q29,
  output Q30,
  output Q31,
  output Q0
);

  USR_1BIT usr_1bit_1 (
    .Shift_Right(Q1), .Shift_Left(Shift_Left), .CLK(Clk), .Parallel_Load(P0), .S1(S1), .S0(S0), .out_8(Q0));  // open: No_Connection, Q_bar
  USR_1BIT usr_1bit_2 (
    .Shift_Right(Q2), .Shift_Left(Q0), .CLK(Clk), .Parallel_Load(P1), .S1(S1), .S0(S0), .out_8(Q1));  // open: No_Connection, Q_bar
  USR_1BIT usr_1bit_3 (
    .Shift_Right(Q3), .Shift_Left(Q1), .CLK(Clk), .Parallel_Load(P2), .S1(S1), .S0(S0), .out_8(Q2));  // open: No_Connection, Q_bar
  USR_1BIT usr_1bit_4 (
    .Shift_Right(Q4), .Shift_Left(Q2), .CLK(Clk), .Parallel_Load(P3), .S1(S1), .S0(S0), .out_8(Q3));  // open: No_Connection, Q_bar
  USR_1BIT usr_1bit_5 (
    .Shift_Right(Q5), .Shift_Left(Q3), .CLK(Clk), .Parallel_Load(P4), .S1(S1), .S0(S0), .out_8(Q4));  // open: No_Connection, Q_bar
  USR_1BIT usr_1bit_6 (
    .Shift_Right(Q6), .Shift_Left(Q4), .CLK(Clk), .Parallel_Load(P5), .S1(S1), .S0(S0), .out_8(Q5));  // open: No_Connection, Q_bar
  USR_1BIT usr_1bit_7 (
    .Shift_Right(Q7), .Shift_Left(Q5), .CLK(Clk), .Parallel_Load(P6), .S1(S1), .S0(S0), .out_8(Q6));  // open: No_Connection, Q_bar
  USR_1BIT usr_1bit_8 (
    .Shift_Right(Q8), .Shift_Left(Q6), .CLK(Clk), .Parallel_Load(P7), .S1(S1), .S0(S0), .out_8(Q7));  // open: No_Connection, Q_bar
  USR_1BIT usr_1bit_9 (
    .Shift_Right(Q9), .Shift_Left(Q7), .CLK(Clk), .Parallel_Load(P8), .S1(S1), .S0(S0), .out_8(Q8));  // open: No_Connection, Q_bar
  USR_1BIT usr_1bit_10 (
    .Shift_Right(Q10), .Shift_Left(Q8), .CLK(Clk), .Parallel_Load(P9), .S1(S1), .S0(S0), .out_8(Q9));  // open: No_Connection, Q_bar
  USR_1BIT usr_1bit_11 (
    .Shift_Right(Q11), .Shift_Left(Q9), .CLK(Clk), .Parallel_Load(P10), .S1(S1), .S0(S0), .out_8(Q10));  // open: No_Connection, Q_bar
  USR_1BIT usr_1bit_12 (
    .Shift_Right(Q12), .Shift_Left(Q10), .CLK(Clk), .Parallel_Load(P11), .S1(S1), .S0(S0), .out_8(Q11));  // open: No_Connection, Q_bar
  USR_1BIT usr_1bit_13 (
    .Shift_Right(Q13), .Shift_Left(Q11), .CLK(Clk), .Parallel_Load(P12), .S1(S1), .S0(S0), .out_8(Q12));  // open: No_Connection, Q_bar
  USR_1BIT usr_1bit_14 (
    .Shift_Right(Q14), .Shift_Left(Q12), .CLK(Clk), .Parallel_Load(P13), .S1(S1), .S0(S0), .out_8(Q13));  // open: No_Connection, Q_bar
  USR_1BIT usr_1bit_15 (
    .Shift_Right(Q15), .Shift_Left(Q13), .CLK(Clk), .Parallel_Load(P14), .S1(S1), .S0(S0), .out_8(Q14));  // open: No_Connection, Q_bar
  USR_1BIT usr_1bit_16 (
    .Shift_Right(Q16), .Shift_Left(Q14), .CLK(Clk), .Parallel_Load(P15), .S1(S1), .S0(S0), .out_8(Q15));  // open: No_Connection, Q_bar
  USR_1BIT usr_1bit_17 (
    .Shift_Right(Q17), .Shift_Left(Q15), .CLK(Clk), .Parallel_Load(P16), .S1(S1), .S0(S0), .out_8(Q16));  // open: No_Connection, Q_bar
  USR_1BIT usr_1bit_18 (
    .Shift_Right(Q18), .Shift_Left(Q16), .CLK(Clk), .Parallel_Load(P17), .S1(S1), .S0(S0), .out_8(Q17));  // open: No_Connection, Q_bar
  USR_1BIT usr_1bit_19 (
    .Shift_Right(Q19), .Shift_Left(Q17), .CLK(Clk), .Parallel_Load(P18), .S1(S1), .S0(S0), .out_8(Q18));  // open: No_Connection, Q_bar
  USR_1BIT usr_1bit_20 (
    .Shift_Right(Q20), .Shift_Left(Q18), .CLK(Clk), .Parallel_Load(P19), .S1(S1), .S0(S0), .out_8(Q19));  // open: No_Connection, Q_bar
  USR_1BIT usr_1bit_21 (
    .Shift_Right(Q21), .Shift_Left(Q19), .CLK(Clk), .Parallel_Load(P20), .S1(S1), .S0(S0), .out_8(Q20));  // open: No_Connection, Q_bar
  USR_1BIT usr_1bit_22 (
    .Shift_Right(Q22), .Shift_Left(Q20), .CLK(Clk), .Parallel_Load(P21), .S1(S1), .S0(S0), .out_8(Q21));  // open: No_Connection, Q_bar
  USR_1BIT usr_1bit_23 (
    .Shift_Right(Q23), .Shift_Left(Q21), .CLK(Clk), .Parallel_Load(P22), .S1(S1), .S0(S0), .out_8(Q22));  // open: No_Connection, Q_bar
  USR_1BIT usr_1bit_24 (
    .Shift_Right(Q24), .Shift_Left(Q22), .CLK(Clk), .Parallel_Load(P23), .S1(S1), .S0(S0), .out_8(Q23));  // open: No_Connection, Q_bar
  USR_1BIT usr_1bit_25 (
    .Shift_Right(Q25), .Shift_Left(Q23), .CLK(Clk), .Parallel_Load(P24), .S1(S1), .S0(S0), .out_8(Q24));  // open: No_Connection, Q_bar
  USR_1BIT usr_1bit_26 (
    .Shift_Right(Q26), .Shift_Left(Q24), .CLK(Clk), .Parallel_Load(P25), .S1(S1), .S0(S0), .out_8(Q25));  // open: No_Connection, Q_bar
  USR_1BIT usr_1bit_27 (
    .Shift_Right(Q27), .Shift_Left(Q25), .CLK(Clk), .Parallel_Load(P26), .S1(S1), .S0(S0), .out_8(Q26));  // open: No_Connection, Q_bar
  USR_1BIT usr_1bit_28 (
    .Shift_Right(Q28), .Shift_Left(Q26), .CLK(Clk), .Parallel_Load(P27), .S1(S1), .S0(S0), .out_8(Q27));  // open: No_Connection, Q_bar
  USR_1BIT usr_1bit_29 (
    .Shift_Right(Q29), .Shift_Left(Q27), .CLK(Clk), .Parallel_Load(P28), .S1(S1), .S0(S0), .out_8(Q28));  // open: No_Connection, Q_bar
  USR_1BIT usr_1bit_30 (
    .Shift_Right(Q30), .Shift_Left(Q28), .CLK(Clk), .Parallel_Load(P29), .S1(S1), .S0(S0), .out_8(Q29));  // open: No_Connection, Q_bar
  USR_1BIT usr_1bit_31 (
    .Shift_Right(Q31), .Shift_Left(Q29), .CLK(Clk), .Parallel_Load(P30), .S1(S1), .S0(S0), .out_8(Q30));  // open: No_Connection, Q_bar
  USR_1BIT usr_1bit_32 (
    .Shift_Right(Shift_Right), .Shift_Left(Q30), .CLK(Clk), .Parallel_Load(P31), .S1(S1), .S0(S0), .out_8(Q31));  // open: No_Connection, Q_bar

  // Notes on the sheet:
  //   32-Bit Universal Shift Register 
endmodule
